# Fritzing sketch greenthunb_schematic (saved by Fritzing 0.9.3b)

parts:
  U1 = ESP8266 NodeMCU LoLin module
  Grove1 = Grove OLED 128x96
  DS1 = DS18B20 1-Wire Temperature Sensor [part_number=DS18B20]
  Mod1 = KY-019 5V Relay Module [package="Breakout board"]
  Part1 = BH1750
  Part2 = Soil Moisture Sensor
  DHT1 = DHT11 Humitidy and Temperature Sensor

nets:
  N1: U1.D1, Part1.SCL
  N2: U1.D2, Part1.SDA
  N3: U1.D4, DS1.DQ
  VCC: U1.3V3, Grove1.VCC, DS1.VDD, Mod1.+, Part1.VCC, Part2.VCC, DHT1.VDD
  N4: U1.D6, Mod1.S
  N5: U1.D7, Grove1.SCL
  N6: U1.D8, Grove1.SDA
  GND: U1.GND, Grove1.GND, DS1.GND, Mod1.-, Part1.GND, Part2.GND, DHT1.GND
  N7: U1.S3, DHT1.DATA
  N8: U1.A0, Part2.SIG

custom parts:
  ESP8266 NodeMCU LoLin module: ESP8266 based NodeMCU
  KY-019 5V Relay Module: KY-019 5V Relay module, used to control AC circuits. (Special thanks to vanepp for fixing the PCB holes and other errors)
  BH1750: Light Sensor
  DHT11 Humitidy and Temperature Sensor: DHT11 Humidity and Temperature Sensor
